# Fritzing sketch NewGagandeepN01305833 (saved by Fritzing 0.9.4)
circuit board: 8.47cm x 5.64444cm
breadboards: 1

parts:
  Raspberry_Pi_1 = Raspberry Pi 3 [part_number=RPI-3-V1.2]
  Part1 = Digital Temperature Sensor Breakout - TMP102
  R1 = Resistor [tolerance=±5% resistance=330 package=THT]
  Q1 = NPN-Transistor [package="TO92 [THT]"]
  JP1 = Header 6 [package=molex-1x6-ra]
  R2 = Resistor [tolerance=±5% resistance=56k package=THT]
  LED1 = LED - 5mm [color="Red (633nm)" package="5 mm [THT]"]

nets:
  3.3V: Raspberry_Pi_1.3v3, Raspberry_Pi_1.3V3, Part1.V+, R1.Pin_0, JP1.2
  SDA: Raspberry_Pi_1.GPIO2, Part1.SDA, JP1.3
  SCL: Raspberry_Pi_1.GPIO3, Part1.SCL, JP1.4
  GND: Raspberry_Pi_1.GND, Part1.GND, Q1.E, JP1.1
  GPIO26: Raspberry_Pi_1.GPIO26, R2.Pin_0
  ALT: Part1.ALERT, JP1.5
  ADD0: Part1.ADD0, JP1.6
  N1: R1.Pin_1, LED1.anode
  N2: Q1.B, R2.Pin_1
  N3: Q1.C, LED1.cathode
